# Fritzing sketch mouse (saved by Fritzing 0.9.2b)

parts:
  Teensy1 = Teensy 3.6 (Basic)
  Part2 = Adafruit TB6612 DC and Stepper Motor Driver [part_number="Adafruit #2448"]
  M1 = DC Motor  # not connected
  M2 = DC Motor  # not connected
  U1 = LIPO-110mAh [package=lipo-110]
  Part3 = Adafruit VL6180X Time of Flight Distance Sensor [part_number="Adafruit #3316"]
  Part4 = Adafruit VL6180X Time of Flight Distance Sensor [part_number="Adafruit #3316"]

nets:
  GND: Teensy1.GND, Teensy1.GND1, U1.-
  3V3: Teensy1.3V3, Teensy1.3V3_1, Part2.VCC
  N1: Teensy1.AGND, Part2.GND
  N2: Teensy1.Vin, U1.+
  N3: Part2.Vmotor, Part2.PWRIN
  VIN: Part3.VIN, Part4.VIN

custom parts:
  Teensy 3.6 (Basic): The Teensy is a complete USB-based microcontoller development system, in a very small footprint, capable of implementing many types of projects. All programming is done via the USB port. No special programmer is needed, only a standard micro-USB cable and a PC or Macintosh with a USB port.
  Adafruit TB6612 DC and Stepper Motor Driver: Spin two DC motors, step one bi-polar or uni-polar stepper, or fire off two solenoids with 1.2A per channel using the TB6612. These are perhaps better known as "the drivers in our assembled Adafruit Motorshield or Motor HAT." We really like these dual H-bridges, so if you want to control motors without a shield or HAT these are easy to include on any solderless breadboard or perma-proto.
  Adafruit VL6180X Time of Flight Distance Sensor: The VL6180X is a Time of Flight distance sensor like no other you've used! The sensor contains a very tiny invisible laser source, and a matching sensor. The VL6180X can detect the "time of flight", or how long the light has taken to bounce back to the sensor. Since it uses a very narrow light source, it is good for determining distance of only the surface directly in front of it. Unlike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
